// Logisim project 8BitBenEater.circ as structural Verilog: 8 circuits, main circuit main
module main (
  input  in_1,
  input  in_2,
  input  in_3,
  input  PROGRAM_MODE
);

  wire bcd_to_7_segment_decoder_2_p1, bcd_to_7_segment_decoder_3_p1, binary_to_bcd_converter_1_p2,
       clock_1_out, mar_1_p1, mar_1_p5, not_1_out;
  wire [3:0] dipswitch_1_sw4, mar_1_p2, mar_1_p3, multiplexer_1_out;
  wire [7:0] binary_to_bcd_converter_1_p1, register_a_1_always_out, register_b_1_always_out;
  wire [7:4] pull_resistor_4_node;

  LED led_1 (.in(not_1_out));
  not not_1 (not_1_out, PROGRAM_MODE);
  DipSwitch #(.number(4)) dipswitch_1 (
    .sw1(dipswitch_1_sw4[3]), .sw2(dipswitch_1_sw4[2]), .sw3(dipswitch_1_sw4[1]), .sw4(dipswitch_1_sw4[0]));
  LED led_2 (.in(PROGRAM_MODE));
  Clock clock_1 (.out(clock_1_out));
  Multiplexer #(.width(4)) multiplexer_1 (
    .in0(mar_1_p2), .in1(dipswitch_1_sw4), .out(multiplexer_1_out), .sel(PROGRAM_MODE));
  // MAR mar_1: pin names not known; wires that end beside it: mar_1_p1, mar_1_p2, mar_1_p3, mar_1_p3, mar_1_p5, mar_1_p5
  LED led_3 (.in(multiplexer_1_out[3]));
  LED led_4 (.in(multiplexer_1_out[2]));
  LED led_5 (.in(multiplexer_1_out[1]));
  LED led_6 (.in(multiplexer_1_out[0]));
  CLK clk_1 (.CLK_IN(clock_1_out), .CLK_ENB(in_1), .CLK_MANUAL(in_2), .HALT(in_3), .CLK_OUT(mar_1_p1));
  LED led_7 (.in(pull_resistor_4_node[7]));
  LED led_8 (.in(pull_resistor_4_node[6]));
  LED led_9 (.in(pull_resistor_4_node[5]));
  LED led_10 (.in(pull_resistor_4_node[4]));
  Pull_Resistor pull_resistor_1 (.node(pull_resistor_4_node[7]));
  Pull_Resistor pull_resistor_2 (.node(pull_resistor_4_node[6]));
  Pull_Resistor pull_resistor_3 (.node(pull_resistor_4_node[5]));
  Pull_Resistor pull_resistor_4 (.node(pull_resistor_4_node[4]));
  LED led_11 (.in(mar_1_p3[3]));
  LED led_12 (.in(mar_1_p3[2]));
  LED led_13 (.in(mar_1_p3[1]));
  LED led_14 (.in(mar_1_p3[0]));
  Pull_Resistor pull_resistor_5 (.node(mar_1_p3[3]));
  Pull_Resistor pull_resistor_6 (.node(mar_1_p3[2]));
  Pull_Resistor pull_resistor_7 (.node(mar_1_p3[1]));
  Pull_Resistor pull_resistor_8 (.node(mar_1_p3[0]));
  PROGRAM_COUNTER program_counter_1 (
    .CLOCK(mar_1_p1), .ADDRESS_IN(mar_1_p3), .ADDRESS_OUT(mar_1_p3));  // open: RESET, JUMP, COUNTER_ENABLE, COUNTER_OUT, ALWAYS_OUT
  REGISTER_A register_a_1 (
    .DATA_IN({pull_resistor_4_node, mar_1_p3}), .CLOCK(mar_1_p1), .ALWAYS_OUT(register_a_1_always_out),
    .DATA_OUT({pull_resistor_4_node, mar_1_p3}));  // open: A_IN, A_OUT, A_RESET
  REGISTER_B register_b_1 (
    .CLOCK(mar_1_p1), .DATA_IN({pull_resistor_4_node, mar_1_p3}), .ALWAYS_OUT(register_b_1_always_out));  // open: B_IN, B_OUT, RESET, DATA_OUT
  _7_Segment_Display u_7_segment_display_1 ();  // open: g, f, a, b, e, d, c, dp
  _7_Segment_Display u_7_segment_display_2 ();  // open: g, f, a, b, e, d, c, dp
  // BCD_to_7_Segment_decoder bcd_to_7_segment_decoder_1: pin names not known
  // BCD_to_7_Segment_decoder bcd_to_7_segment_decoder_2: pin names not known; wires that end beside it: bcd_to_7_segment_decoder_2_p1
  // Binary_to_BCD_converter #(.binvalue(8)) binary_to_bcd_converter_1: pin names not known; wires that end beside it: binary_to_bcd_converter_1_p1, binary_to_bcd_converter_1_p2, binary_to_bcd_converter_1_p2, bcd_to_7_segment_decoder_2_p1
  OUTPUT_REGISTER output_register_1 (
    .CLOCK(mar_1_p1), .DATA_IN({pull_resistor_4_node, mar_1_p3}), .DATA_OUT(binary_to_bcd_converter_1_p1));  // open: STORE, RESET
  ALU alu_1 (
    .A_IN(register_a_1_always_out), .B_IN(register_b_1_always_out),
    .ALU_DATA_OUT({pull_resistor_4_node, mar_1_p3}));  // open: OUTPUT_ENB, SUB, ALWAYS_OUT, COUT
  _7_Segment_Display u_7_segment_display_3 ();  // open: g, f, a, b, e, d, c, dp
  // BCD_to_7_Segment_decoder bcd_to_7_segment_decoder_3: pin names not known; wires that end beside it: bcd_to_7_segment_decoder_3_p1, bcd_to_7_segment_decoder_3_p1
endmodule

module CLK (
  input  CLK_IN,
  input  CLK_ENB,
  input  CLK_MANUAL,
  input  HALT,
  output CLK_OUT
);

  wire and_1_out, and_2_out, not_1_out, not_2_out, or_1_out;

  not not_1 (not_1_out, CLK_ENB);
  not not_2 (not_2_out, HALT);
  and and_1 (and_1_out, CLK_IN, CLK_ENB);
  and and_2 (and_2_out, not_1_out, CLK_MANUAL);
  or or_1 (or_1_out, and_1_out, and_2_out);
  and and_3 (CLK_OUT, or_1_out, not_2_out);
endmodule

module PROGRAM_COUNTER (
  input  RESET,
  input  JUMP,
  input  COUNTER_ENABLE,
  input  CLOCK,
  input  [3:0] ADDRESS_IN,
  input  COUNTER_OUT,
  output [3:0] ALWAYS_OUT,
  output [3:0] ADDRESS_OUT
);

  Counter #(.max('hf), .width(4)) counter_1 (
    .clr(RESET), .load(JUMP), .up(COUNTER_ENABLE), .count(COUNTER_ENABLE), .clk(CLOCK), .D(ADDRESS_IN),
    .Q(ALWAYS_OUT));  // open: carry
  assign ADDRESS_OUT = COUNTER_OUT ? ALWAYS_OUT : 4'bz;  // Controlled_Buffer controlled_buffer_1
endmodule

module REGISTER_A (
  input  [7:0] DATA_IN,
  input  A_IN,
  input  A_OUT,
  input  CLOCK,
  input  A_RESET,
  output [7:0] ALWAYS_OUT,
  output [7:0] DATA_OUT
);

  Register register_1 (.D(DATA_IN), .en(A_IN), .clk(CLOCK), .Q(ALWAYS_OUT), .clr(A_RESET));
  assign DATA_OUT = A_OUT ? ALWAYS_OUT : 8'bz;  // Controlled_Buffer controlled_buffer_1
endmodule

module ALU (
  input  [7:0] A_IN,
  input  [7:0] B_IN,
  input  OUTPUT_ENB,
  input  SUB,
  output [7:0] ALWAYS_OUT,
  output [7:0] ALU_DATA_OUT,
  output COUT
);

  wire not_1_out;
  wire [7:0] controlled_buffer_1_out, xor_1_out;

  assign controlled_buffer_1_out = SUB ? {8{1'b1}} : 8'bz;  // Controlled_Buffer controlled_buffer_1
  assign controlled_buffer_1_out = not_1_out ? {8{1'b0}} : 8'bz;  // Controlled_Buffer controlled_buffer_2
  not not_1 (not_1_out, SUB);
  assign xor_1_out = B_IN ^ controlled_buffer_1_out;  // XOR_Gate xor_1, 8 bits wide
  Adder adder_1 (.a(A_IN), .b(xor_1_out), .out(ALWAYS_OUT), .cin(SUB), .cout(COUT));
  assign ALU_DATA_OUT = OUTPUT_ENB ? ALWAYS_OUT : 8'bz;  // Controlled_Buffer controlled_buffer_3
endmodule

module REGISTER_B (
  input  [7:0] DATA_IN,
  input  B_IN,
  input  B_OUT,
  input  CLOCK,
  input  RESET,
  output [7:0] ALWAYS_OUT,
  output [7:0] DATA_OUT
);

  Register register_1 (.D(DATA_IN), .en(B_IN), .clk(CLOCK), .Q(ALWAYS_OUT), .clr(RESET));
  assign DATA_OUT = B_OUT ? ALWAYS_OUT : 8'bz;  // Controlled_Buffer controlled_buffer_1
endmodule

module OUTPUT_REGISTER (
  input  [7:0] DATA_IN,
  input  STORE,
  input  CLOCK,
  input  RESET,
  output [7:0] DATA_OUT
);

  Register register_1 (.D(DATA_IN), .en(STORE), .clk(CLOCK), .Q(DATA_OUT), .clr(RESET));
endmodule

module MAR (
  input  [3:0] DATA_IN,
  input  MAR_IN,
  input  MAR_OUT,
  input  CLOCK,
  input  MAR_RESET,
  output [3:0] ALWAYS_OUT,
  output [3:0] DATA_OUT
);

  Register #(.width(4)) register_1 (.D(DATA_IN), .en(MAR_IN), .clk(CLOCK), .Q(ALWAYS_OUT), .clr(MAR_RESET));
  assign DATA_OUT = MAR_OUT ? ALWAYS_OUT : 4'bz;  // Controlled_Buffer controlled_buffer_1
endmodule
